# Fritzing sketch Master (saved by Fritzing 0.9.2b)
breadboards: 1

parts:
  Part1 = CT-UNO
  LED1 = LED - 5mm [color="Red (633nm)" package="5 mm [THT]"]
  LED2 = LED - 5mm [color="Red (633nm)" package="5 mm [THT]"]
  R1 = Resistor [tolerance=±5% resistance=220 package=THT]
  R2 = Resistor [tolerance=±5% resistance=220 package=THT]
  J1 = Basic Servo

nets:
  N1: Part1.no_name_yet#52, R1.Pin_1
  N2: Part1.no_name_yet#56, R2.Pin_1
  N3: Part1.no_name_yet#87, J1.vcc
  N4: Part1.no_name_yet#88, LED1.cathode, LED2.cathode, J1.gnd
  N5: LED1.anode, R1.Pin_0
  N6: LED2.anode, R2.Pin_0
