# Fritzing sketch Slave (saved by Fritzing 0.9.2b)
breadboards: 1

parts:
  Part1 = CT-UNO
  R1 = Rotary Potentiometer (Small) [maximum_resistance=100kΩ package=THT]
  R2 = Rotary Potentiometer (Small) [maximum_resistance=100kΩ package=THT]
  S1 = Pushbutton [package=THT]
  R3 = Resistor [tolerance=±5% resistance=10k package=THT]

nets:
  N1: Part1.no_name_yet#0, R1.wiper
  N2: Part1.no_name_yet#1, S1.leg0, R3.Pin_0
  N3: Part1.no_name_yet#2, R2.wiper
  N4: Part1.no_name_yet#87, R1.leg1, R2.leg1, R3.Pin_1
  N5: Part1.no_name_yet#89, R1.leg2, R2.leg2, S1.leg1
